# Fritzing sketch schema (saved by Fritzing 0.9.4)
breadboards: 1

parts:
  Part1 = Arduino Uno (Rev3)
  LED1 = LED - 5mm [color="Red (633nm)" package="5 mm [THT]"]
  LED2 = LED - 5mm [color="Red (633nm)" package="5 mm [THT]"]
  S1 = Pushbutton [package="[THT]"]
  J1 = Basic Servo
  R1 = Resistor [tolerance=±5% resistance=220 package=THT]

nets:
  N1: Part1.D9_PWM, J1.pulse
  N2: Part1.D3_PWM, R1.Pin_1
  N3: Part1.D7, S1.Pin_3, S1.Pin_4
  5V: Part1.5V, J1.vcc
  GND: Part1.GND, LED1.cathode, S1.Pin_1, S1.Pin_2, J1.gnd
  N4: LED1.anode, LED2.cathode
  N5: LED2.anode, R1.Pin_0

notes:
  Future improvement: 3 leds per cannon.
  Future improvement: add 2 servo motors (1 per cannon)
